# Fritzing sketch CCLAB_Arduino_Final (saved by Fritzing 0.9.0b)
breadboards: 1

parts:
  Part1 = Arduino Uno (Rev3)
  R1 = Resistor [tolerance=±5% resistance=220 package=THT]
  R2 = Photocell (LDR) [package=THT]
  J1 = Piezo Speaker
  J2 = Basic Servo
  J3 = Basic Servo
  LED1 = LED - 5mm [color="Red (633nm)" package="5 mm [THT]"]
  J4 = Infrared Proximity Sensor

nets:
  N1: Part1.A5/SCL, R1.Pin_1, R2.pin_0
  N2: Part1.D9_PWM, J2.pulse, J3.pulse
  N3: Part1.D13/SCK, LED1.cathode
  N4: Part1.D6_PWM, J1.pin2
  N5: Part1.D7, J4.Vout
  VCC: Part1.5V, R2.pin_1, J2.vcc, J3.vcc, J4.Vcc
  GND: Part1.GND, R1.Pin_0, J1.pin1, J2.gnd, J3.gnd, LED1.anode, J4.GND
